// Logisim project ALU-Control.circ as structural Verilog: 1 circuit, main circuit main
module main (
  input  [2:0] ALUop,
  input  Func_7,
  input  [2:0] Func_3,
  output [4:0] ALU_Control
);

  wire and_1_out, and_2_out, and_3_out, and_4_out, and_5_out, and_6_out, and_7_out, and_8_out, and_9_out,
       and_10_out, and_11_out, and_12_out, not_1_out, not_2_out, not_3_out, not_4_out, not_5_out, not_6_out,
       not_7_out, not_8_out, not_9_out, not_10_out, not_11_out, not_12_out, not_13_out, not_14_out,
       not_15_out, not_16_out, not_17_out, not_18_out, not_19_out;
  wire [3:0] priority_encoder_1_out;

  not not_1 (not_1_out, ALUop[2]);
  not not_2 (not_2_out, ALUop[2]);
  not not_3 (not_3_out, ALUop[0]);
  not not_4 (not_4_out, ALUop[2]);
  not not_5 (not_5_out, ALUop[1]);
  not not_6 (not_6_out, ALUop[0]);
  not not_7 (not_7_out, Func_7);
  not not_8 (not_8_out, ALUop[1]);
  not not_9 (not_9_out, ALUop[0]);
  not not_10 (not_10_out, ALUop[2]);
  not not_11 (not_11_out, ALUop[0]);
  not not_12 (not_12_out, ALUop[1]);
  not not_13 (not_13_out, ALUop[2]);
  not not_14 (not_14_out, ALUop[2]);
  not not_15 (not_15_out, ALUop[1]);
  not not_16 (not_16_out, Func_3[1]);
  not not_17 (not_17_out, ALUop[2]);
  not not_18 (not_18_out, ALUop[1]);
  and and_1 (and_1_out, ALUop[0], not_1_out, ALUop[1]);
  and and_2 (and_2_out, not_2_out, ALUop[1], not_3_out);
  and and_3 (and_3_out, not_4_out, not_5_out, not_6_out, not_7_out);
  and and_4 (and_4_out, not_8_out, not_9_out, Func_7, not_10_out);
  and and_5 (and_5_out, not_11_out, not_12_out, not_13_out);
  and and_6 (and_6_out, not_14_out, not_15_out, ALUop[0]);
  and and_7 (and_7_out, Func_3[2], not_16_out, Func_3[0]);
  and and_8 (and_8_out, not_17_out, not_18_out, ALUop[0]);
  not not_19 (not_19_out, Func_7);
  and and_9 (and_9_out, and_6_out, not_19_out, and_7_out);
  and and_10 (and_10_out, and_6_out, and_7_out, Func_7);
  and and_11 (and_11_out, and_6_out, and_7_out);
  Priority_Encoder #(.select(4)) priority_encoder_1 (
    .in0(and_1_out), .in1(and_2_out), .in2(and_3_out), .in3(and_4_out), .in4(and_5_out), .in5(and_9_out),
    .in6(and_10_out), .in7(and_11_out), .in8(and_8_out), .in9(and_12_out), .out(priority_encoder_1_out));  // open: in10, in11, in12, in13, in14, in15, gs, en_out, en_in
  and and_12 (and_12_out, and_1_out, and_2_out, and_3_out, and_4_out, and_5_out, and_9_out, and_10_out, and_11_out, and_8_out);
  Multiplexer #(.select(4), .width(5)) multiplexer_1 (
    .in0({5{1'b1}}), .in1({2'b10, Func_3}), .in2({2'b00, Func_3}), .in3({2'b01, Func_3}),
    .in4({2'b00, Func_3}), .in5({2'b00, Func_3}), .in6({2'b01, Func_3}), .in7({2'b00, Func_3}),
    .in8({2'b00, Func_3}), .in9({5{1'b0}}), .out(ALU_Control), .sel(priority_encoder_1_out));  // open: in10, in11, in12, in13, in14, in15, en

  // Notes on the sheet:
  //   ALU CONTROL
endmodule
