// Logisim project ALU.circ as structural Verilog: 1 circuit, main circuit main
module main (
  input  [31:0] in_1,
  input  [31:0] in_2,
  input  [4:0] ALU_Control,
  output [31:0] out_4,
  output out_5
);

  wire comparator_1_eq, comparator_1_gt, comparator_1_lt, comparator_2_eq, comparator_2_gt, comparator_2_lt,
       comparator_3_eq, comparator_3_lt, comparator_4_eq, comparator_5_eq, not_1_out, or_1_out, or_3_out;
  wire [31:0] adder_1_out, and_1_out, multiplexer_1_out, multiplexer_2_out, multiplexer_3_out,
       multiplexer_4_out, multiplexer_5_out, multiplexer_6_out, multiplexer_7_out, or_2_out, shifter_1_out,
       shifter_2_out, shifter_3_out, subtractor_1_out, xor_1_out;

  Adder #(.width(32)) adder_1 (.a(in_1), .b(in_2), .out(adder_1_out));  // open: cin, cout
  Shifter #(.width(32)) shifter_1 (.in(in_1), .\dist (in_2[4:0]), .out(shifter_1_out));
  Comparator #(.width(32)) comparator_1 (
    .a(in_1), .b(in_2), .gt(comparator_1_gt), .eq(comparator_1_eq), .lt(comparator_1_lt));
  assign xor_1_out = in_1 ^ in_2;  // XOR_Gate xor_1, 32 bits wide
  Shifter #(.width(32), .shift("lr")) shifter_2 (.in(in_1), .\dist (in_2[4:0]), .out(shifter_2_out));
  or or_1 (or_1_out, comparator_1_gt, comparator_1_eq);
  assign or_2_out = in_1 | in_2;  // OR_Gate or_2, 32 bits wide
  assign and_1_out = in_1 & in_2;  // AND_Gate and_1, 32 bits wide
  Subtractor #(.width(32)) subtractor_1 (.a(in_1), .b(in_2), .out(subtractor_1_out));  // open: bin, bout
  Shifter #(.width(32), .shift("ar")) shifter_3 (.in(in_1), .\dist (in_2[4:0]), .out(shifter_3_out));
  Comparator #(.width(32)) comparator_2 (
    .a(in_1), .b(in_2), .gt(comparator_2_gt), .eq(comparator_2_eq), .lt(comparator_2_lt));
  not not_1 (not_1_out, comparator_3_eq);
  Comparator #(.width(32)) comparator_3 (.a(in_1), .b(in_2), .eq(comparator_3_eq), .lt(comparator_3_lt));  // open: gt
  Multiplexer #(.width(32)) multiplexer_1 (
    .in0({32{1'b0}}), .in1(32'h1), .out(multiplexer_1_out), .sel(comparator_1_lt));  // open: en
  Multiplexer #(.width(32)) multiplexer_2 (
    .in0({32{1'b0}}), .in1(32'h1), .out(multiplexer_2_out), .sel(comparator_1_eq));  // open: en
  or or_3 (or_3_out, comparator_2_gt, comparator_2_eq);
  Multiplexer #(.width(32)) multiplexer_3 (
    .in0({32{1'b0}}), .in1(32'h1), .out(multiplexer_3_out), .sel(or_1_out));  // open: en
  Multiplexer #(.width(32)) multiplexer_4 (
    .in0({32{1'b0}}), .in1(32'h1), .out(multiplexer_4_out), .sel(or_3_out));  // open: en
  Multiplexer #(.width(32)) multiplexer_5 (
    .in0({32{1'b0}}), .in1(32'h1), .out(multiplexer_5_out), .sel(comparator_2_lt));  // open: en
  Multiplexer #(.width(32)) multiplexer_6 (
    .in0({32{1'b0}}), .in1(32'h1), .out(multiplexer_6_out), .sel(not_1_out));  // open: en
  Multiplexer #(.width(32)) multiplexer_7 (
    .in0({32{1'b0}}), .in1(32'h1), .out(multiplexer_7_out), .sel(comparator_3_lt));  // open: en
  Multiplexer #(.select(5), .width(32)) multiplexer_8 (
    .in0(adder_1_out), .in1(shifter_1_out), .in2(multiplexer_1_out), .in3(multiplexer_5_out),
    .in4(xor_1_out), .in5(shifter_2_out), .in6(or_2_out), .in7(and_1_out), .in8(subtractor_1_out),
    .in13(shifter_3_out), .in16(multiplexer_2_out), .in17(multiplexer_6_out), .in20(multiplexer_7_out),
    .in21(multiplexer_3_out), .in22(multiplexer_5_out), .in23(multiplexer_4_out), .in31(in_1), .out(out_4),
    .sel(ALU_Control));  // open: in9, in10, in11, in12, in14, in15, in18, in19, in24, in25, in26, in27, in28, in29, in30, en
  Comparator #(.width(32)) comparator_4 (.a(32'h1), .b(out_4), .eq(comparator_4_eq));  // open: gt, lt
  Comparator #(.width(2)) comparator_5 (.a(ALU_Control[4:3]), .b(2'b10), .eq(comparator_5_eq));  // open: gt, lt
  and and_2 (out_5, comparator_4_eq, comparator_5_eq);

  // Notes on the sheet:
  //   A
  //   B
  //   JAL,JALR
  //   ALU
  //   ADD,ADDI
  //   SLL,SLLI
  //   XOR,XORI
  //   SRL,SRLI
  //   OR,ORI
  //   SLT,SLTI
  //   BEQ
  //   BGE
  //   AND,ANDI
  //   SUB
  //   SRA,SRAI
  //   BGEU
  //   SLTU,SLTUI,BLTU
  //   BNE
  //   BLT
  //   Output
  //   BRANCH
endmodule
