// Logisim project ALUop.circ as structural Verilog: 1 circuit, main circuit main
module main (
  input  R_Format,
  input  Store,
  input  Load,
  input  I_Type,
  input  Branch,
  input  Lui,
  input  JAL,
  input  JALR,
  output [2:0] out_9
);

  wire not_1_out, or_1_out, or_2_out;

  or or_1 (or_1_out, JAL, JALR);
  or or_2 (or_2_out, R_Format, Store, Load, I_Type, Branch, Lui, JAL, JALR);
  not not_1 (not_1_out, or_2_out);
  // AND_Gate and_1 has open pins: in0=R_Format, in1=Store, in2=Load, in3=I_Type, in4=Branch, in5=Lui, in6=JAL, in7=JALR, out=open
  Priority_Encoder priority_encoder_1 (
    .in0(R_Format), .in1(I_Type), .in2(Branch), .in3(or_1_out), .in4(Load), .in5(Store), .in6(Lui),
    .in7(not_1_out), .out(out_9));  // open: en_in, gs, en_out
endmodule
