// Logisim project Control Decode.circ as structural Verilog: 1 circuit, main circuit main
module main (
  input  R_Format,
  input  Store,
  input  Load,
  input  I_Type,
  input  Branch,
  input  Lui,
  input  JAL,
  input  JALR,
  output Memwrite,
  output Branch_2,
  output Memread,
  output RegWrite,
  output MemtoReg,
  output [2:0] AluOp,
  output [1:0] Operand_sel_A,
  output Operand_sel_B,
  output [1:0] Extend_sel,
  output [1:0] Next_PC_select
);

  or or_1 (RegWrite, R_Format, Load, I_Type, JALR, JAL, Lui);
  ALUop_main main_1 (
    .R_Format(R_Format), .Store(Store), .Load(Load), .I_Type(I_Type), .Branch(Branch), .Lui(Lui), .JAL(JAL),
    .JALR(JALR), .out_9(AluOp));
  Operand_sel_A_main main_2 (.Lui(Lui), .JAL(JAL), .JALR(JALR), .out_4(Operand_sel_A));
  Next_Pc_Select_main main_3 (.Jr(JALR), .J(JAL), .B(Branch), .out_4(Next_PC_select));
  or or_2 (Operand_sel_B, I_Type, Lui, Store, Load);

  assign Branch_2 = Branch;
  assign Extend_sel = {Store, Lui};
  assign Memread = Load;
  assign MemtoReg = Load;
  assign Memwrite = Store;
endmodule
