// Logisim project Control Unit1.circ as structural Verilog: 1 circuit, main circuit main
module main (
  input  [6:0] Opcode,
  output MemWrite,
  output Branch,
  output MemRead,
  output RegWrite,
  output MemtoReg,
  output [2:0] ALUop,
  output Operand_B_Sel,
  output [1:0] Operand_A_Sel,
  output [1:0] Extend_Sel,
  output [1:0] Next_PC_Sel
);

  wire main_1_branch, main_1_i_type, main_1_jal, main_1_jalr, main_1_load, main_1_lui, main_1_r_format,
       main_1_store;

  Type_Decode_main main_1 (
    .Opcode(Opcode), .R_Format(main_1_r_format), .Store(main_1_store), .Load(main_1_load),
    .I_Type(main_1_i_type), .Branch(main_1_branch), .Lui(main_1_lui), .JAL(main_1_jal), .JALR(main_1_jalr));
  Control_Decode_main main_2 (
    .R_Format(main_1_r_format), .Store(main_1_store), .Load(main_1_load), .I_Type(main_1_i_type),
    .Branch(main_1_branch), .Lui(main_1_lui), .JAL(main_1_jal), .JALR(main_1_jalr), .Memwrite(MemWrite),
    .Branch_2(Branch), .Memread(MemRead), .RegWrite(RegWrite), .MemtoReg(MemtoReg), .AluOp(ALUop),
    .Operand_sel_A(Operand_A_Sel), .Operand_sel_B(Operand_B_Sel), .Extend_sel(Extend_Sel),
    .Next_PC_select(Next_PC_Sel));

  // Notes on the sheet:
  //   Control Unit
  //   R-Format
  //   Store
  //   Load
  //   I-Type
  //   Branch
  //   LUI
  //   JAL
  //   JALR
endmodule
