// Logisim project Immediate Generation.circ as structural Verilog: 1 circuit, main circuit main
module main (
  input  [31:0] in_1,
  input  [31:0] in_2,
  output [31:0] out_3,
  output [31:0] out_4,
  output [31:0] out_5,
  output [31:0] out_6,
  output [31:0] out_7
);

  wire [31:0] bit_extender_3_out, bit_extender_4_out, bit_extender_5_out, shifter_1_out, shifter_2_out;

  assign out_3 = {{20{in_1[31]}}, in_1[31:20]};  // Bit_Extender bit_extender_1
  assign out_4 = {{20{in_1[31]}}, {in_1[31:25], in_1[11:7]}};  // Bit_Extender bit_extender_2
  assign bit_extender_3_out = {{12{in_1[31]}}, in_1[31:12]};  // Bit_Extender bit_extender_3
  assign bit_extender_4_out = {{11{in_1[31]}}, {in_1[31], in_1[19:12], in_1[20], in_1[30:21], 1'b0}};  // Bit_Extender bit_extender_4
  assign bit_extender_5_out = {{19{in_1[31]}}, {in_1[31], in_1[7], in_1[30:25], in_1[11:8], 1'b0}};  // Bit_Extender bit_extender_5
  Shifter #(.width(32)) shifter_1 (.in(bit_extender_4_out), .\dist (5'b00001), .out(shifter_1_out));
  Shifter #(.width(32)) shifter_2 (.in(bit_extender_5_out), .\dist (5'b00001), .out(shifter_2_out));
  Shifter #(.width(32)) shifter_3 (.in(bit_extender_3_out), .\dist (5'b01100), .out(out_6));
  Adder #(.width(32)) adder_1 (.a(shifter_2_out), .b(in_2), .out(out_5));  // open: cin, cout
  Adder #(.width(32)) adder_2 (.a(shifter_1_out), .b(in_2), .out(out_7));  // open: cin, cout

  // Notes on the sheet:
  //   Instruction
  //   PC
  //   I-immediate
  //   S-immediate
  //   SB-Immediate
  //   U-Immediate
  //   UJ-Immediate
endmodule
