// Logisim project JALR-target.circ as structural Verilog: 1 circuit, main circuit main
module main (
  input  [31:0] in_1,
  input  [31:0] in_2,
  output [31:0] out_3
);

  wire [31:0] adder_1_out;

  Adder #(.width(32)) adder_1 (.a(in_1), .b(in_2), .out(adder_1_out));  // open: cin, cout
  assign out_3 = 32'hfffffffe & adder_1_out;  // AND_Gate and_1, 32 bits wide

  // Notes on the sheet:
  //   JALR-Target
endmodule
