// Logisim project Next_Pc_Select 1.circ as structural Verilog: 1 circuit, main circuit main
module main (
  input  Jr,
  input  J,
  input  B,
  output [1:0] out_4
);

  wire xnor_1_out;

  NotExactlyOne xnor_1 (.out(xnor_1_out), .in0(Jr), .in1(B), .in2(J));
  Priority_Encoder #(.select(2)) priority_encoder_1 (
    .in0(xnor_1_out), .in1(B), .in2(J), .in3(Jr), .out(out_4));  // open: gs, en_out, en_in

  // Notes on the sheet:
  //   NEXT_PC_Select
endmodule
