// Logisim project Next_Pc_Select.circ as structural Verilog: 1 circuit, main circuit main
module main (
  input  Jr,
  input  J,
  input  B,
  output [1:0] out_4
);

  wire and_1_out, and_2_out, and_3_out, and_4_out, not_1_out, not_2_out, not_3_out, not_4_out, not_5_out,
       not_6_out, not_7_out, not_8_out;

  not not_1 (not_1_out, Jr);
  not not_2 (not_2_out, J);
  not not_3 (not_3_out, Jr);
  not not_4 (not_4_out, B);
  not not_5 (not_5_out, J);
  not not_6 (not_6_out, B);
  not not_7 (not_7_out, J);
  not not_8 (not_8_out, B);
  and and_1 (and_1_out, not_1_out, not_2_out, B);
  and and_2 (and_2_out, not_3_out, J, not_4_out);
  and and_3 (and_3_out, Jr, not_5_out, not_6_out);
  and and_4 (and_4_out, Jr, not_7_out, not_8_out);
  or or_1 (out_4[0], and_1_out, and_3_out);
  or or_2 (out_4[1], and_2_out, and_4_out);

  // Notes on the sheet:
  //   NEXT_PC_Select
endmodule
