// Logisim project Operand_sel_A.circ as structural Verilog: 1 circuit, main circuit main
module main (
  input  Lui,
  input  JAL,
  input  JALR,
  output [1:0] out_4
);

  wire and_1_out, and_2_out, and_3_out, not_1_out, not_2_out, not_3_out, not_4_out, not_5_out, not_6_out,
       not_7_out, not_8_out;

  not not_1 (not_1_out, Lui);
  not not_2 (not_2_out, JAL);
  not not_3 (not_3_out, Lui);
  not not_4 (not_4_out, JALR);
  not not_5 (not_5_out, JAL);
  not not_6 (not_6_out, JALR);
  not not_7 (not_7_out, JAL);
  not not_8 (not_8_out, JALR);
  and and_1 (and_1_out, not_1_out, not_2_out, JALR);
  and and_2 (and_2_out, not_3_out, JAL, not_4_out);
  and and_3 (and_3_out, Lui, not_5_out, not_6_out);
  and and_4 (out_4[0], Lui, not_7_out, not_8_out);
  or or_1 (out_4[1], and_1_out, and_2_out, and_3_out);

  // Notes on the sheet:
  //   Operand_sel_A
endmodule
