// Logisim project lab6.circ as structural Verilog: 1 circuit, main circuit main
module main (
  input  [31:0] Instruction_32_bit,
  input  [31:0] in_2,
  input  [31:0] in_3,
  output [31:0] out_4
);

  wire comparator_1_lt, comparator_2_lt, comparator_3_eq, comparator_4_eq, comparator_5_eq, comparator_6_eq,
       comparator_7_eq, comparator_8_eq, comparator_9_eq, comparator_10_eq, comparator_11_eq;
  wire [2:0] priority_encoder_1_out;
  wire [31:0] adder_1_out, and_1_out, multiplexer_1_out, multiplexer_2_out, multiplexer_3_out,
       multiplexer_4_out, or_1_out, shifter_1_out, shifter_2_out, shifter_3_out, subtractor_1_out, xor_1_out;

  Adder #(.width(32)) adder_1 (.a(in_3), .b(in_2), .out(adder_1_out));  // open: cin, cout
  Subtractor #(.width(32)) subtractor_1 (.a(in_3), .b(in_2), .out(subtractor_1_out));  // open: bin, bout
  Shifter #(.width(32)) shifter_1 (.in(in_3), .\dist (in_2[4:0]), .out(shifter_1_out));
  Comparator #(.width(32)) comparator_1 (.a(in_3), .lt(comparator_1_lt));  // open: b, gt, eq
  Comparator #(.width(32), .mode("unsigned")) comparator_2 (.a(in_3), .lt(comparator_2_lt));  // open: b, gt, eq
  assign xor_1_out = in_3 ^ in_2;  // XOR_Gate xor_1, 32 bits wide
  Shifter #(.width(32), .shift("lr")) shifter_2 (.in(in_3), .\dist (in_2[4:0]), .out(shifter_2_out));
  Shifter #(.width(32), .shift("ar")) shifter_3 (.in(in_3), .\dist (in_2[4:0]), .out(shifter_3_out));
  assign or_1_out = in_3 | in_2;  // OR_Gate or_1, 32 bits wide
  assign and_1_out = in_3 & in_2;  // AND_Gate and_1, 32 bits wide
  Multiplexer #(.width(32), .enable("false")) multiplexer_1 (
    .in0({32{1'b0}}), .in1(32'h1), .out(multiplexer_1_out), .sel(comparator_1_lt));
  Multiplexer #(.width(32), .enable("false")) multiplexer_2 (
    .in0({32{1'b0}}), .in1(32'h1), .out(multiplexer_2_out), .sel(comparator_2_lt));
  // Probe on Instruction_32_bit[14:12]
  Multiplexer #(.width(32), .disabled(0), .enable("false")) multiplexer_3 (
    .in0(adder_1_out), .in1(subtractor_1_out), .out(multiplexer_3_out), .sel(Instruction_32_bit[30]));
  Multiplexer #(.width(32), .enable("false")) multiplexer_4 (
    .in0(shifter_2_out), .in1(shifter_3_out), .out(multiplexer_4_out), .sel(Instruction_32_bit[30]));
  // Probe on Instruction_32_bit[6:0]
  // Probe on {Instruction_32_bit[31], Instruction_32_bit[29:25]}
  // Probe on Instruction_32_bit[30]
  Multiplexer #(.select(3), .width(32), .disabled(0), .enable("false")) multiplexer_5 (
    .in0(multiplexer_3_out), .in1(shifter_1_out), .in2(multiplexer_1_out), .in3(multiplexer_2_out),
    .in4(xor_1_out), .in5(multiplexer_4_out), .in6(or_1_out), .in7(and_1_out), .out(out_4),
    .sel(priority_encoder_1_out));
  Comparator #(.width(7)) comparator_3 (
    .a(Instruction_32_bit[6:0]), .b(7'b0110011), .eq(comparator_3_eq));  // open: gt, lt
  Comparator #(.width(3)) comparator_4 (
    .a(Instruction_32_bit[14:12]), .b(3'b000), .eq(comparator_4_eq));  // open: gt, lt
  Comparator #(.width(3)) comparator_5 (
    .a(Instruction_32_bit[14:12]), .b(3'b001), .eq(comparator_5_eq));  // open: gt, lt
  Comparator #(.width(3)) comparator_6 (
    .a(Instruction_32_bit[14:12]), .b(3'b010), .eq(comparator_6_eq));  // open: gt, lt
  Comparator #(.width(3)) comparator_7 (
    .a(Instruction_32_bit[14:12]), .b(3'b011), .eq(comparator_7_eq));  // open: gt, lt
  Comparator #(.width(3)) comparator_8 (
    .a(Instruction_32_bit[14:12]), .b(3'b100), .eq(comparator_8_eq));  // open: gt, lt
  Comparator #(.width(3)) comparator_9 (
    .a(Instruction_32_bit[14:12]), .b(3'b101), .eq(comparator_9_eq));  // open: gt, lt
  Comparator #(.width(3)) comparator_10 (
    .a(Instruction_32_bit[14:12]), .b(3'b110), .eq(comparator_10_eq));  // open: gt, lt
  Comparator #(.width(3)) comparator_11 (
    .a(Instruction_32_bit[14:12]), .b(3'b111), .eq(comparator_11_eq));  // open: gt, lt
  Priority_Encoder priority_encoder_1 (
    .in0(comparator_4_eq), .in1(comparator_5_eq), .in2(comparator_6_eq), .in3(comparator_7_eq),
    .in4(comparator_8_eq), .in5(comparator_9_eq), .in6(comparator_10_eq), .in7(comparator_11_eq),
    .out(priority_encoder_1_out), .en_in(comparator_3_eq));  // open: gs, en_out
  // Probe on priority_encoder_1_out

  // Notes on the sheet:
  //   ALU ENABLE
endmodule
