// Logisim project Type Decode.circ as structural Verilog: 1 circuit, main circuit main
module main (
  input  [6:0] Opcode,
  output R_Format,
  output Store,
  output Load,
  output I_Type,
  output Branch,
  output Lui,
  output JAL,
  output JALR
);

  Comparator #(.width(7)) comparator_1 (.a(7'b0110011), .b(Opcode), .eq(R_Format));  // open: gt, lt
  Comparator #(.width(7)) comparator_2 (.a(Opcode), .b(7'b0100011), .eq(Store));  // open: gt, lt
  Comparator #(.width(7)) comparator_3 (.a(Opcode), .b(7'b0000011), .eq(Load));  // open: gt, lt
  Comparator #(.width(7)) comparator_4 (.a(Opcode), .b(7'b0010011), .eq(I_Type));  // open: gt, lt
  Comparator #(.width(7)) comparator_5 (.a(Opcode), .b(7'b1100011), .eq(Branch));  // open: gt, lt
  Comparator #(.width(7)) comparator_6 (.a(Opcode), .b(7'b0110111), .eq(Lui));  // open: gt, lt
  Comparator #(.width(7)) comparator_7 (.a(Opcode), .b(7'b1101111), .eq(JAL));  // open: gt, lt
  Comparator #(.width(7)) comparator_8 (.a(Opcode), .b(7'b1100111), .eq(JALR));  // open: gt, lt
endmodule
